// Logisim project dot86.circ as structural Verilog: 6 circuits, main circuit cpu
module cpu (
);

  wire and_1_out, and_2_out, and_3_out, and_4_out, buffer_1_out, buffer_2_out, buffer_3_out, CLK_out,
       CTRL_UNIT_alu, CTRL_UNIT_disp8, CTRL_UNIT_disp32, CTRL_UNIT_imm8, CTRL_UNIT_imm32, CTRL_UNIT_m32,
       CTRL_UNIT_mem_read, CTRL_UNIT_mem_write, CTRL_UNIT_reg_write, CTRL_UNIT_rm, CTRL_UNIT_rr, nor_1_out,
       not_1_out, or_1_out, RESET_out, xor_1_out;
  wire [2:0] CTRL_UNIT_alu_fun, CTRL_UNIT_left_reg, CTRL_UNIT_right_reg;
  wire [7:0] INS_MEM_disp8, INS_MEM_imm8, INS_MEM_modrm, INS_MEM_op;
  wire [15:0] CTRL_UNIT_pc_out, multiplexer_1_out, PC_q;
  wire [31:0] adder_1_out, bit_extender_1_out, bit_extender_2_out, demultiplexer_1_out0,
       demultiplexer_1_out1, demultiplexer_2_out0, demultiplexer_2_out1, demultiplexer_3_out0,
       demultiplexer_3_out1, demultiplexer_6_out1, demultiplexer_7_out1, INS_MEM_disp32, INS_MEM_imm32,
       multiplexer_2_out, multiplexer_3_out, multiplexer_4_out, multiplexer_5_out, RA_MEM_data_out,
       REG_FILE_left_out, undriven, undriven_2;

  Button RESET (.out(RESET_out));
  buf buffer_1 (buffer_1_out, RESET_out);
  buf buffer_2 (buffer_2_out, buffer_1_out);
  Clock CLK (.out(CLK_out));
  or or_1 (or_1_out, RESET_out, buffer_3_out);
  buf buffer_3 (buffer_3_out, buffer_2_out);
  Multiplexer #(.width(16)) multiplexer_1 (
    .in0(CTRL_UNIT_pc_out), .in1(16'h400), .out(multiplexer_1_out), .sel(or_1_out));
  Register #(.width(16)) PC (.D(multiplexer_1_out), .en(1'b1), .clk(xor_1_out), .Q(PC_q));  // open: clr
  xor xor_1 (xor_1_out, buffer_3_out, CLK_out);
  instruction_memory INS_MEM (
    .ADDR(PC_q), .CLK(xor_1_out), .OP(INS_MEM_op), .MODRM(INS_MEM_modrm), .IMM8(INS_MEM_imm8),
    .IMM32(INS_MEM_imm32), .DISP8(INS_MEM_disp8), .DISP32(INS_MEM_disp32));  // open: DATA, WRT
  control_unit CTRL_UNIT (
    .OP(INS_MEM_op), .MODRM(INS_MEM_modrm), .PC(PC_q), .GOTO(INS_MEM_imm32), .ALU_FUN(CTRL_UNIT_alu_fun),
    .ALU(CTRL_UNIT_alu), .REG_WRITE(CTRL_UNIT_reg_write), .MEM_READ(CTRL_UNIT_mem_read),
    .MEM_WRITE(CTRL_UNIT_mem_write), .LEFT_REG(CTRL_UNIT_left_reg), .RIGHT_REG(CTRL_UNIT_right_reg),
    .RR(CTRL_UNIT_rr), .IMM8(CTRL_UNIT_imm8), .IMM32(CTRL_UNIT_imm32), .M32(CTRL_UNIT_m32),
    .RM(CTRL_UNIT_rm), .DISP8(CTRL_UNIT_disp8), .DISP32(CTRL_UNIT_disp32), .PC_OUT(CTRL_UNIT_pc_out));
  assign bit_extender_1_out = {{24{1'b0}}, INS_MEM_imm8};  // Bit_Extender bit_extender_1
  Demultiplexer #(.width(32)) demultiplexer_1 (
    .out0(demultiplexer_1_out0), .out1(demultiplexer_1_out1), .in(demultiplexer_2_out0), .sel(CTRL_UNIT_rr));
  Demultiplexer #(.width(32)) demultiplexer_2 (
    .out0(demultiplexer_2_out0), .out1(demultiplexer_2_out1), .in(undriven), .sel(CTRL_UNIT_alu));
  assign bit_extender_2_out = {{24{1'b0}}, INS_MEM_disp8};  // Bit_Extender bit_extender_2
  nor nor_1 (nor_1_out, CTRL_UNIT_m32, CTRL_UNIT_rm);
  Demultiplexer #(.width(32)) demultiplexer_3 (
    .out0(demultiplexer_3_out0), .out1(demultiplexer_3_out1), .in(demultiplexer_1_out0), .sel(nor_1_out));
  register_file REG_FILE (
    .DATA(undriven), .WRT(CTRL_UNIT_reg_write), .LEFT_REG(CTRL_UNIT_left_reg),
    .RIGHT_REG(CTRL_UNIT_right_reg), .RESET(or_1_out), .CLK(xor_1_out), .LEFT_OUT(REG_FILE_left_out),
    .RIGHT_OUT(demultiplexer_1_out1));
  and and_1 (and_1_out, CTRL_UNIT_imm8, ~CTRL_UNIT_imm32);  // AND_Gate
  Demultiplexer #(.width(32)) demultiplexer_4 (
    .out0(INS_MEM_imm32), .out1(bit_extender_1_out), .in(demultiplexer_3_out1), .sel(and_1_out));
  Demultiplexer #(.width(32)) demultiplexer_5 (
    .out0(INS_MEM_imm32), .out1(bit_extender_1_out), .in(demultiplexer_6_out1), .sel(and_1_out));
  Demultiplexer #(.width(32)) demultiplexer_6 (
    .out0(demultiplexer_3_out0), .out1(demultiplexer_6_out1), .in(demultiplexer_7_out1), .sel(nor_1_out));
  not not_1 (not_1_out, CTRL_UNIT_rr);
  Demultiplexer #(.width(32)) demultiplexer_7 (
    .out0(demultiplexer_1_out1), .out1(demultiplexer_7_out1), .in(undriven_2), .sel(not_1_out));
  and and_2 (and_2_out, CTRL_UNIT_disp8, CTRL_UNIT_disp32);
  and and_3 (and_3_out, CTRL_UNIT_disp32, ~CTRL_UNIT_disp8);  // AND_Gate
  Multiplexer #(.width(32)) multiplexer_2 (
    .in0(bit_extender_2_out), .in1(INS_MEM_disp32), .out(multiplexer_2_out), .sel(and_3_out));
  arithmetic_logic_unit ALU (
    .L_OPERAND(REG_FILE_left_out), .R_OPERAND(undriven_2), .FUNC(CTRL_UNIT_alu_fun),
    .RESULT(demultiplexer_2_out1));  // open: ZERO, NEGATIVE, CARRY, OVERFLOW
  Adder #(.width(32)) adder_1 (
    .a(demultiplexer_1_out1), .b(multiplexer_2_out), .out(adder_1_out), .cin(1'b0));  // open: cout
  and and_4 (and_4_out, CTRL_UNIT_rm, ~and_2_out, ~CTRL_UNIT_rr);  // AND_Gate
  Multiplexer #(.width(32)) multiplexer_3 (
    .in0(adder_1_out), .in1(demultiplexer_1_out1), .out(multiplexer_3_out), .sel(and_4_out));
  Multiplexer #(.width(32)) multiplexer_4 (
    .in0(REG_FILE_left_out), .in1(demultiplexer_2_out1), .out(multiplexer_4_out), .sel(CTRL_UNIT_rm));
  Multiplexer #(.width(32)) multiplexer_5 (
    .in0(multiplexer_3_out), .in1(INS_MEM_disp32), .out(multiplexer_5_out), .sel(CTRL_UNIT_m32));
  assign demultiplexer_3_out0 = CTRL_UNIT_mem_read ? RA_MEM_data_out : 32'bz;  // Controlled_Buffer controlled_buffer_1
  random_access_memory RA_MEM (
    .ADDR(multiplexer_5_out), .WRT(CTRL_UNIT_mem_write), .CLK(xor_1_out), .DATA(multiplexer_4_out),
    .DATA_OUT(RA_MEM_data_out));  // open: OUT_OF_RANGE
endmodule

module instruction_memory (
  input  [15:0] ADDR,
  input  [47:0] DATA,
  input  WRT,
  input  CLK,
  output [7:0] OP,
  output [7:0] MODRM,
  output [7:0] IMM8,
  output [31:0] IMM32,
  output [7:0] DISP8,
  output [31:0] DISP32
);

  RAM #(.addrWidth(16), .dataWidth(48), .enables("line")) INS_MEM (
    .addr(ADDR), .we(WRT), .clk(CLK), .din(DATA), .dout({OP, IMM8, DISP32[31:8], DISP8}));

  assign DISP32[7:0] = DISP8;
  assign IMM32 = {DISP32[23:8], DISP8, IMM8};
  assign MODRM = IMM8;
endmodule

module register_file (
  input  [31:0] DATA,
  input  WRT,
  input  [2:0] LEFT_REG,
  input  [2:0] RIGHT_REG,
  input  RESET,
  input  CLK,
  output [31:0] LEFT_OUT,
  output [31:0] RIGHT_OUT
);

  wire undriven, undriven_2, undriven_3, undriven_4, undriven_5, undriven_6, undriven_7, undriven_8;
  wire [31:0] BP_q, DI_q, RA_q, RB_q, RC_q, RD_q, SI_q, SP_q;

  Multiplexer #(.select(3)) multiplexer_1 (
    .in0(undriven), .in1(undriven_2), .in2(undriven_3), .in3(undriven_4), .in4(undriven_5), .in5(undriven_6),
    .in6(undriven_7), .in7(undriven_8), .out(WRT), .sel(LEFT_REG));
  Register #(.width(32)) RA (.D(DATA), .en(undriven), .clk(CLK), .Q(RA_q), .clr(RESET));
  Register #(.width(32)) RB (.D(DATA), .en(undriven_2), .clk(CLK), .Q(RB_q), .clr(RESET));
  Register #(.width(32)) RC (.D(DATA), .en(undriven_3), .clk(CLK), .Q(RC_q), .clr(RESET));
  Register #(.width(32)) RD (.D(DATA), .en(undriven_4), .clk(CLK), .Q(RD_q), .clr(RESET));
  Register #(.width(32)) SP (.D(DATA), .en(undriven_5), .clk(CLK), .Q(SP_q), .clr(RESET));
  Register #(.width(32)) BP (.D(DATA), .en(undriven_6), .clk(CLK), .Q(BP_q), .clr(RESET));
  Register #(.width(32)) SI (.D(DATA), .en(undriven_7), .clk(CLK), .Q(SI_q), .clr(RESET));
  Register #(.width(32)) DI (.D(DATA), .en(undriven_8), .clk(CLK), .Q(DI_q), .clr(RESET));
  Demultiplexer #(.select(3), .width(32)) demultiplexer_1 (
    .out0(RA_q), .out1(RB_q), .out2(RC_q), .out3(RD_q), .out4(SP_q), .out5(BP_q), .out6(SI_q), .out7(DI_q),
    .in(LEFT_OUT), .sel(LEFT_REG));
  Demultiplexer #(.select(3), .width(32)) demultiplexer_2 (
    .out0(RA_q), .out1(RB_q), .out2(RC_q), .out3(RD_q), .out4(SP_q), .out5(BP_q), .out6(SI_q), .out7(DI_q),
    .in(RIGHT_OUT), .sel(RIGHT_REG));
endmodule

module control_unit (
  input  [7:0] OP,
  input  [7:0] MODRM,
  input  [15:0] PC,
  input  [31:0] GOTO,
  output [2:0] ALU_FUN,
  output ALU,
  output REG_WRITE,
  output MEM_READ,
  output MEM_WRITE,
  output [2:0] LEFT_REG,
  output [2:0] RIGHT_REG,
  output RR,
  output IMM8,
  output IMM32,
  output M32,
  output RM,
  output DISP8,
  output DISP32,
  output [15:0] PC_OUT
);

  wire ADD_out, and_1_out, and_2_out, and_3_out, and_4_out, and_5_out, and_6_out, and_7_out, and_8_out,
       and_9_out, and_10_out, disp_out, nand_1_out, or_1_out, or_2_out, or_4_out, or_6_out, xor_1_out;
  wire [15:0] adder_1_out, adder_2_out, adder_3_out, multiplexer_1_out, multiplexer_3_out, multiplexer_4_out;

  Multiplexer #(.width(16)) multiplexer_1 (.in0(16'h1), .in1(16'h2), .out(multiplexer_1_out), .sel(or_1_out));
  Adder #(.width(16)) adder_1 (.a(PC), .b(multiplexer_1_out), .out(adder_1_out), .cin(1'b0));  // open: cout
  nand nand_1 (nand_1_out, MODRM[6], MODRM[7]);
  and and_1 (and_1_out, MODRM[6], MODRM[7]);
  buf or_1 (or_1_out, ~and_4_out);  // OR_Gate OR_Gate
  and ADD (ADD_out, ~OP[2], ~OP[3], ~OP[4], ~OP[5], ~OP[6], ~OP[7]);  // AND_Gate
  and and_2 (and_2_out, MODRM[6], ~and_1_out);  // AND_Gate
  and and_3 (and_3_out, MODRM[7], ~and_1_out);  // AND_Gate
  and and_4 (and_4_out, OP[1], ADD_out);
  buf or_2 (or_2_out, and_4_out);  // OR_Gate
  Multiplexer #(.width(3)) multiplexer_2 (.in0(MODRM[2:0]), .in1(3'b000), .out(RIGHT_REG), .sel(or_2_out));
  xor xor_1 (xor_1_out, and_2_out, and_3_out);
  and and_5 (and_5_out, MODRM[0], ~MODRM[1], MODRM[2], nand_1_out);  // AND_Gate
  and and_6 (and_6_out, xor_1_out, and_3_out);
  and and_7 (and_7_out, OP[0], and_4_out, ADD_out);
  buf or_3 (IMM32, and_7_out);  // OR_Gate
  and and_8 (and_8_out, OP[0], ~OP[1], ADD_out);  // AND_Gate
  or or_4 (or_4_out, and_5_out, IMM32, and_6_out);
  or disp (disp_out, and_3_out, and_2_out);
  Multiplexer #(.width(16)) multiplexer_3 (.in0({16{1'b0}}), .in1(16'h4), .out(multiplexer_3_out), .sel(or_4_out));
  and and_9 (and_9_out, ~OP[0], and_4_out, ADD_out);  // AND_Gate
  Adder #(.width(16)) adder_2 (.a(adder_1_out), .b(multiplexer_3_out), .out(adder_2_out), .cin(1'b0));  // open: cout
  buf or_5 (IMM8, and_9_out);  // OR_Gate
  and and_10 (and_10_out, ~and_5_out, disp_out, ~and_6_out, ~and_1_out);  // AND_Gate
  Multiplexer #(.width(16)) multiplexer_4 (.in0({16{1'b0}}), .in1(16'h1), .out(multiplexer_4_out), .sel(or_6_out));
  or or_6 (or_6_out, IMM8, and_10_out);
  and and_11 (RR, or_1_out, and_1_out);
  and and_12 (M32, and_5_out, ~disp_out, or_1_out);  // AND_Gate
  and and_13 (RM, ~and_5_out, ~disp_out, ~and_1_out, or_1_out);  // AND_Gate
  and and_14 (DISP8, ~and_6_out, disp_out, or_1_out);  // AND_Gate
  and and_15 (DISP32, and_6_out, disp_out, or_1_out);
  Adder #(.width(16)) adder_3 (.a(adder_2_out), .b(multiplexer_4_out), .out(adder_3_out), .cin(1'b0));  // open: cout
  Multiplexer #(.width(16)) multiplexer_5 (.in0(adder_3_out), .in1(GOTO[15:0]), .out(PC_OUT), .sel(1'b0));
  Priority_Encoder priority_encoder_1 (
    .in0(ADD_out), .out(ALU_FUN), .en_in(1'b1), .gs(ALU));  // open: in1, in2, in3, in4, in5, in6, in7, en_out
  buf or_7 (REG_WRITE, ADD_out);  // OR_Gate
  buf or_8 (MEM_READ, RM);  // OR_Gate
  buf or_9 (MEM_WRITE, and_8_out);  // OR_Gate

  assign LEFT_REG = MODRM[5:3];

  // Notes on the sheet:
  //   modrm?
  //   use RA reg?
  //   imm32?
  //   imm8?
  //   jump?
endmodule

module arithmetic_logic_unit (
  input  [31:0] L_OPERAND,
  input  [31:0] R_OPERAND,
  input  [2:0] FUNC,
  output [31:0] RESULT,
  output ZERO,
  output NEGATIVE,
  output CARRY,
  output OVERFLOW
);

  wire [31:0] adder_1_out;

  Adder #(.width(32)) adder_1 (.a(L_OPERAND), .b(R_OPERAND), .out(adder_1_out));  // open: cin, cout
  Multiplexer #(.select(3), .width(32)) multiplexer_1 (
    .in0(adder_1_out), .out(RESULT), .sel(FUNC));  // open: in1, in2, in3, in4, in5, in6, in7
endmodule

module random_access_memory (
  input  [31:0] ADDR,
  input  WRT,
  input  CLK,
  input  [31:0] DATA,
  output OUT_OF_RANGE,
  output [31:0] DATA_OUT
);

  RAM #(.addrWidth(24), .dataWidth(32), .enables("line")) RA_M (
    .addr(ADDR[23:0]), .we(WRT), .clk(CLK), .din(DATA), .dout(DATA_OUT));

  assign OUT_OF_RANGE = 1'b0;

  // Notes on the sheet:
  //   todo: check if out of range
endmodule
